# Fritzing sketch TiefpassAktiv (saved by Fritzing 0.9.9b)
breadboards: 1

parts:
  IC1 = TL072 [package="DIP (Dual Inline) [THT]"]
  IC1_PWR = TL072 [package="DIP (Dual Inline) [THT]"]  # not connected
  IC1_A = TL072 [package="DIP (Dual Inline) [THT]"]  # not connected
  IC1_B = TL072 [package="DIP (Dual Inline) [THT]"]  # not connected
  C1 = Ceramic Capacitor [capacitance=100nF voltage=35V package="100 mil [THT, multilayer]"]
  R1 = Resistor [tolerance=±5% power=0.25 resistance=10k package=THT]
  C2 = Ceramic Capacitor [capacitance=100nF voltage=35V package="100 mil [THT, multilayer]"]
  R2 = Resistor [tolerance=±5% power=0.25 resistance=10k package=THT]
  C3 = Electrolytic Capacitor [capacitance=1µF voltage=35V package="100 mil [THT, electrolytic]"]
  C4 = Electrolytic Capacitor [capacitance=1µF voltage=35V package="100 mil [THT, electrolytic]"]
  VM1 = Multimeter (DC Voltage)
  P1 = Multimeter straight red probe
  P2 = Multimeter straight black probe

nets:
  N1: IC1.connector0, R1.Pin_1, C2.1, VM1.V_Probe, P1.Probe_tip, P1.Probe_meter_end
  N2: IC1.connector1, R1.Pin_0, C2.0, R2.Pin_0
  N3: IC1.connector2, C3.-, C4.+, VM1.COM_Probe, P2.Probe_tip, P2.Probe_meter_end, P2.Probe_tip_2
  N4: IC1.connector3, C1.0, C3.+
  N5: IC1.connector7, C1.1, C4.-

custom parts:
  TL072: Dual Operational Amplifier
  TL072: Dual Operational Amplifier
  TL072: Dual Operational Amplifier
  TL072: Dual Operational Amplifier
