# Fritzing sketch universalfilter (saved by Fritzing 0.9.9b)
breadboards: 1

parts:
  IC2_B = TL072 [package="DIP (Dual Inline) [THT]"]  # not connected
  IC2_A = TL072 [package="DIP (Dual Inline) [THT]"]  # not connected
  IC2_PWR = TL072 [package="DIP (Dual Inline) [THT]"]  # not connected
  IC2 = TL072 [package="DIP (Dual Inline) [THT]"]
  C5 = Electrolytic Capacitor [capacitance=1µF voltage=35V package="100 mil [THT, electrolytic]"]
  C6 = Electrolytic Capacitor [capacitance=1µF voltage=35V package="100 mil [THT, electrolytic]"]
  C7 = Ceramic Capacitor [capacitance=100nF voltage=35V package="100 mil [THT, multilayer]"]
  IC3 = TL072 [package="DIP (Dual Inline) [THT]"]  # not connected
  IC3_B = TL072 [package="DIP (Dual Inline) [THT]"]  # not connected
  IC3_A = TL072 [package="DIP (Dual Inline) [THT]"]  # not connected
  IC3_PWR = TL072 [package="DIP (Dual Inline) [THT]"]  # not connected
  R2 = Rotary Potentiometer (Small) [maximum_resistance=100kΩ package=THT]

nets:
  N1: IC2.connector1, R2.leg2
  N2: IC2.connector2, R2.leg1
  N3: IC2.connector3, C5.+, C7.0
  N4: IC2.connector7, C6.+, C7.1

custom parts:
  TL072: Dual Operational Amplifier
  TL072: Dual Operational Amplifier
  TL072: Dual Operational Amplifier
  TL072: Dual Operational Amplifier
