# Fritzing sketch amp (saved by Fritzing 1.0.2b)
breadboards: 1

parts:
  C1 = Ceramic Capacitor [capacitance=100nF voltage=35V package="100 mil [THT, multilayer]"]
  C2 = Electrolytic Capacitor [capacitance=1µF voltage=35V package="100 mil [THT, electrolytic]"]
  TL072 = TL072 [package="DIP (Dual Inline) [THT]"]
  TL072_B = TL072 [package="DIP (Dual Inline) [THT]"]  # not connected
  TL072_PWR = TL072 [package="DIP (Dual Inline) [THT]"]
  TL072_A = TL072 [package="DIP (Dual Inline) [THT]"]
  R1 = Resistor [tolerance=±5% power=0.25 resistance=10k package=THT]
  C4 = Ceramic Capacitor [capacitance=100nF voltage=35V package="100 mil [THT, multilayer]"]
  R2 = Resistor [tolerance=±5% power=0.25 resistance=1M package=THT]
  C3 = Electrolytic Capacitor [capacitance=1µF voltage=35V package="100 mil [THT, electrolytic]"]

nets:
  N1: C1.0, TL072.connector3, TL072_PWR.pin4, C3.+
  N2: C1.1, C2.-, TL072.connector7, TL072_PWR.pin8
  GND: C2.+, TL072.connector2, TL072_A.pin3, C3.-
  N3: TL072.connector0, TL072_A.pin1, C4.1, R2.Pin_1
  N4: TL072.connector1, TL072_A.pin2, R1.Pin_0, C4.0, R2.Pin_0

custom parts:
  TL072: Dual Operational Amplifier
  TL072: Dual Operational Amplifier
  TL072: Dual Operational Amplifier
  TL072: Dual Operational Amplifier

// code stored in the sketch: invertedampl.ino
1+1
