# Fritzing sketch sallenkey (saved by Fritzing 0.9.9b)
breadboards: 1

parts:
  IC2_B = TL072 [package="DIP (Dual Inline) [THT]"]  # not connected
  IC2_A = TL072 [package="DIP (Dual Inline) [THT]"]
  IC2_PWR = TL072 [package="DIP (Dual Inline) [THT]"]  # not connected
  IC2 = TL072 [package="DIP (Dual Inline) [THT]"]
  C5 = Ceramic Capacitor [capacitance=100nF voltage=35V package="100 mil [THT, multilayer]"]
  C6 = Ceramic Capacitor [capacitance=100nF voltage=35V package="100 mil [THT, multilayer]"]
  C7 = Electrolytic Capacitor [capacitance=1µF voltage=35V package="100 mil [THT, electrolytic]"]
  C8 = Electrolytic Capacitor [capacitance=1µF voltage=35V package="100 mil [THT, electrolytic]"]
  VM2 = Multimeter (DC Voltage)
  P3 = Multimeter straight red probe
  P4 = Multimeter straight black probe
  R3 = Resistor [tolerance=±5% power=0.25 resistance=5600 package=THT]  # not connected
  R4 = Resistor [tolerance=±5% power=0.25 resistance=10k package=THT]
  C9 = Ceramic Capacitor [capacitance=180nF voltage=35V package="0603 [SMD, multilayer]"]
  R5 = Resistor [tolerance=±5% power=0.25 resistance=330 package=THT]
  R6 = Resistor [tolerance=±5% power=0.25 resistance=2700 package=THT]

nets:
  N1: IC2_A.pin2, IC2.connector1, R5.Pin_1, R6.Pin_0
  N2: IC2.connector0, VM2.V_Probe, P3.Probe_tip, P3.Probe_meter_end, C9.0, R5.Pin_0
  N3: IC2.connector2, C6.0, R4.Pin_0
  N4: IC2.connector3, C5.0, C7.+
  N5: IC2.connector7, C5.1, C8.-
  N6: C6.1, C7.-, C8.+, VM2.COM_Probe, P4.Probe_tip, P4.Probe_meter_end, R6.Pin_1
  N7: R4.Pin_1, C9.1

custom parts:
  TL072: Dual Operational Amplifier
  TL072: Dual Operational Amplifier
  TL072: Dual Operational Amplifier
  TL072: Dual Operational Amplifier
