# Fritzing sketch Dreieck_Rechteck (saved by Fritzing 0.9.9b)
breadboards: 1

parts:
  IC1 = TL072 [package="DIP (Dual Inline) [THT]"]
  元件1 = TL072 [package="DIP (Dual Inline) [THT]"]  # not connected
  IC1_1 = TL072 [package="DIP (Dual Inline) [THT]"]  # not connected
  IC1_2 = TL072 [package="DIP (Dual Inline) [THT]"]  # not connected
  R1 = Resistor [tolerance=±5% power=0.25W resistance=2.7k package=THT]
  R2 = Resistor [tolerance=±10% power=0.25W resistance=10k package=THT]
  C1 = Ceramic Capacitor [capacitance=100nF voltage=35V package="100 mil [THT, multilayer]"]
  R3 = Resistor [tolerance=±5% power=0.25W resistance=22k package=THT]
  C3 = Electrolytic Capacitor [capacitance=1µF voltage=35V package="100 mil [THT, electrolytic]"]
  C4 = Electrolytic Capacitor [capacitance=1µF voltage=35V package="100 mil [THT, electrolytic]"]

nets:
  N1: IC1.connector0, R1.Pin_0, R3.Pin_0
  N2: IC1.connector1, IC1.connector4, C3.+, C4.-
  N3: IC1.connector2, R2.Pin_1, R3.Pin_1
  N4: IC1.connector5, R1.Pin_1, C1.1
  N5: IC1.connector6, R2.Pin_0, C1.0

custom parts:
  TL072: Dual Operational Amplifier
  TL072: Dual Operational Amplifier
  TL072: Dual Operational Amplifier
  TL072: Dual Operational Amplifier
