# Fritzing sketch VCO (saved by Fritzing 1.0.2b)
breadboards: 1

parts:
  IC1 = TL074 Quad Opamp (Movable) [package="DIP (Dual Inline)"]
  元件1 = TL074 Quad Opamp (Movable) [package="DIP (Dual Inline)"]  # not connected
  IC1_1 = TL074 Quad Opamp (Movable) [package="DIP (Dual Inline)"]  # not connected
  IC1_2 = TL074 Quad Opamp (Movable) [package="DIP (Dual Inline)"]  # not connected
  IC1_3 = TL074 Quad Opamp (Movable) [package="DIP (Dual Inline)"]  # not connected
  IC1_4 = TL074 Quad Opamp (Movable) [package="DIP (Dual Inline)"]  # not connected
  C1 = Electrolytic Capacitor [capacitance=1µF voltage=35V package="100 mil [THT, electrolytic]"]
  C2 = Electrolytic Capacitor [capacitance=1µF voltage=35V package="100 mil [THT, electrolytic]"]
  R1 = Resistor [tolerance=±5% power=0.25W resistance=820 package=THT]
  R2 = Resistor [tolerance=±5% power=0.25W resistance=18k package=THT]
  R3 = Resistor [tolerance=±5% power=0.25W resistance=27k package=THT]
  C3 = Ceramic Capacitor [capacitance=100nF voltage=35V package="100 mil [THT, multilayer]"]
  R4 = Resistor [tolerance=±5% power=0.25W resistance=1.2k package=THT]
  R5 = Resistor [tolerance=±5% power=0.25W resistance=1.2k package=THT]
  R6 = Resistor [tolerance=±5% power=0.25W resistance=460 package=THT]
  Q1 = PNP-Transistor [package="TO92 [THT]"]
  Q2 = NPN-Transistor [package="TO92 [THT]"]
  C4 = Ceramic Capacitor [capacitance=100nF voltage=35V package="100 mil [THT, multilayer]"]

nets:
  N1: IC1.connector0, R2.Pin_0, C3.0
  N2: IC1.connector1, R1.Pin_0, C3.1
  N3: IC1.connector2, IC1.connector4, IC1.connector12, C1.+, C2.+
  N4: IC1.connector3, C2.-, C4.1
  N5: IC1.connector5, R4.Pin_0, R5.Pin_0
  N6: IC1.connector6, R5.Pin_1, Q1.E
  N7: IC1.connector7, IC1.connector8, Q2.E
  N8: IC1.connector9, R4.Pin_1
  N9: IC1.connector10, C1.-, C4.0
  N10: IC1.connector11, R2.Pin_1, R3.Pin_1
  N11: IC1.connector13, R1.Pin_1, R3.Pin_0, R6.Pin_1
  N12: R6.Pin_0, Q1.B, Q2.B
  N13: Q1.C, Q2.C

custom parts:
  TL074 Quad Opamp (Movable): Quadruple Operational Amplifier (Opamp)
  TL074 Quad Opamp (Movable): Quadruple Operational Amplifier (Opamp)
  TL074 Quad Opamp (Movable): Quadruple Operational Amplifier (Opamp)
  TL074 Quad Opamp (Movable): Quadruple Operational Amplifier (Opamp)
  TL074 Quad Opamp (Movable): Quadruple Operational Amplifier (Opamp)
  TL074 Quad Opamp (Movable): Quadruple Operational Amplifier (Opamp)
