# Fritzing sketch PI_Filter (saved by Fritzing 1.0.2b)
breadboards: 1

parts:
  U3 = IC4081 [package=dil14]
  IC1 = TL072 [package="DIP (Dual Inline) [THT]"]
  元件2 = TL072 [package="DIP (Dual Inline) [THT]"]  # not connected
  IC1_1 = TL072 [package="DIP (Dual Inline) [THT]"]  # not connected
  IC1_2 = TL072 [package="DIP (Dual Inline) [THT]"]  # not connected
  R1 = Resistor [tolerance=±5% power=0.25W resistance=1k package=THT]
  R2 = Resistor [tolerance=±5% power=0.25W resistance=1k package=THT]
  R3 = Resistor [tolerance=±5% power=0.25W resistance=1k package=THT]
  R4 = Resistor [tolerance=±5% power=0.25W resistance=1k package=THT]
  IC2 = TL072 [package="DIP (Dual Inline) [THT]"]
  元件3 = TL072 [package="DIP (Dual Inline) [THT]"]  # not connected
  IC2_1 = TL072 [package="DIP (Dual Inline) [THT]"]  # not connected
  IC2_2 = TL072 [package="DIP (Dual Inline) [THT]"]  # not connected
  R5 = Resistor [tolerance=±5% power=0.25W resistance=5k package=THT]
  R6 = Resistor [tolerance=±5% power=0.25W resistance=50k package=THT]
  R7 = Resistor [tolerance=±5% power=0.25W resistance=10k package=THT]
  C1 = Tantalum Capacitor [capacitance=1μF voltage=35V package="100 mil [THT, tantalum]"]
  R8 = Resistor [tolerance=±5% power=0.25W resistance=5k package=THT]
  R9 = Resistor [tolerance=±5% power=0.25W resistance=5k package=THT]
  unten = CD4013 [chip_label=IC4013 package="DIP (Dual Inline) [THT]"]
  unten_A = CD4013 [package="DIP (Dual Inline) [THT]"]  # not connected
  unten_B = CD4013 [package="DIP (Dual Inline) [THT]"]  # not connected
  unten_PWR = CD4013 [package="DIP (Dual Inline) [THT]"]  # not connected

nets:
  N1: U3.A1, R3.Pin_0, unten.connector12
  N2: U3.B1, R2.Pin_0, unten.connector0
  N3: U3.Y1, unten.connector3, unten.connector9
  N4: U3.B3, R4.Pin_1, IC2.connector7, R8.Pin_1, unten.connector5, unten.connector6, unten.connector7, unten.connector8, unten.connector13
  N5: IC1.connector0, R1.Pin_0, R5.Pin_0
  N6: IC1.connector1, R1.Pin_1, R2.Pin_1
  N7: IC1.connector2, R3.Pin_1, R4.Pin_0
  N8: IC1.connector3, IC2.connector3
  N9: IC1.connector7, R9.Pin_1, unten.connector4
  N10: IC2.connector0, R6.Pin_0, C1.+
  N11: IC2.connector1, R5.Pin_1, R6.Pin_1, R7.Pin_1
  N12: IC2.connector2, R8.Pin_0, R9.Pin_0
  N13: R7.Pin_0, C1.-

custom parts:
  IC4081: AND GATE
  TL072: Dual Operational Amplifier
  TL072: Dual Operational Amplifier
  TL072: Dual Operational Amplifier
  TL072: Dual Operational Amplifier
  CD4013: CMOS Dual D-Type Flip-Flop
  CD4013: CMOS Dual D-Type Flip-Flop
  CD4013: CMOS Dual D-Type Flip-Flop
  CD4013: CMOS Dual D-Type Flip-Flop
